# Fritzing sketch trashbot_v1.0 (saved by Fritzing 0.9.3b)
breadboards: 1

parts:
  Composant1 = Thumb Joystick
  J1 = Basic Servo
  Composant2 = Arduino Uno (Rev3) - ICSP

nets:
  GND: Composant1.GND, J1.gnd, Composant2.GND
  N1: Composant1.HORZ, Composant2.A2
  VCC: Composant1.VCC, J1.vcc, Composant2.5V
  N2: J1.pulse, Composant2.D3_PWM
